// Digital circuit BatalhaNaval.dig as structural Verilog
module BatalhaNaval (
  input  in_1,
  input  in_2,
  input  in_3,
  input  in_4,
  input  in_5,
  input  in_6,
  input  in_7,
  input  in_8,
  input  in_9,
  input  in_10,
  input  in_11
);

  wire u_batalhaNaval_disparar, u_batalhaNaval_ledg0, u_batalhaNaval_ledg1, u_batalhaNaval_ledg2,
       u_batalhaNaval_ledg3, u_batalhaNaval_ledg4, u_batalhaNaval_ledg5, u_batalhaNaval_ledg6,
       u_batalhaNaval_ledg7, u_batalhaNaval_ledr0, u_batalhaNaval_ledr1, u_batalhaNaval_ledr2,
       u_batalhaNaval_ledr3, u_batalhaNaval_ledr4, u_batalhaNaval_ledr5, undriven, undriven_2, undriven_3;

  batalhaNaval #(.applicationType("GHDL"), .CodeFile("C:\\Users\\User\\Desktop\\faculdade_cc\\3semestre\\sistemasDigitais\\vhdl\\trabalhofinal.vhd")) u_batalhaNaval (
    .sw0(in_1), .sw1(in_3), .sw2(in_2), .sw3(in_4), .sw4(in_11), .sw6(in_10), .sw7(in_5), .sw8(in_6),
    .sw9(in_8), .key1(in_7), .key0(in_9), .ledr5(u_batalhaNaval_ledr5), .ledr4(u_batalhaNaval_ledr4),
    .ledr3(u_batalhaNaval_ledr3), .ledr2(u_batalhaNaval_ledr2), .ledr1(u_batalhaNaval_ledr1),
    .ledr0(u_batalhaNaval_ledr0), .ledg0(u_batalhaNaval_ledg0), .ledg1(u_batalhaNaval_ledg1),
    .ledg2(u_batalhaNaval_ledg2), .ledg3(u_batalhaNaval_ledg3), .ledg4(u_batalhaNaval_ledg4),
    .ledg5(u_batalhaNaval_ledg5), .ledg6(u_batalhaNaval_ledg6), .ledg7(u_batalhaNaval_ledg7),
    .disparar(u_batalhaNaval_disparar));  // open: ledr9, ledr8, ledr7, ledr6
  LED led_1 (.in(u_batalhaNaval_ledr5));
  LED led_2 (.in(u_batalhaNaval_ledr4));
  LED led_3 (.in(u_batalhaNaval_ledr3));
  LED led_4 (.in(u_batalhaNaval_ledr2));
  LED led_5 (.in(u_batalhaNaval_ledr1));
  LED led_6 (.in(u_batalhaNaval_ledr0));
  LED led_7 (.in(u_batalhaNaval_ledg0));
  LED led_8 (.in(u_batalhaNaval_ledg1));
  LED led_9 (.in(u_batalhaNaval_ledg2));
  LED led_10 (.in(u_batalhaNaval_ledg3));
  LED led_11 (.in(u_batalhaNaval_ledg4));
  LED led_12 (.in(u_batalhaNaval_ledg5));
  LED led_13 (.in(u_batalhaNaval_ledg6));
  LED led_14 (.in(u_batalhaNaval_ledg7));
  LED led_15 (.in(u_batalhaNaval_disparar));
  LED led_16 (.in(undriven));
  LED led_17 (.in(undriven_2));
  LED led_18 (.in(undriven_3));

  // Notes on the sheet:
  //   barco
  //   Tiro
endmodule
